# Fritzing sketch Circuit_Tripwire_Alarm_System (saved by Fritzing 0.9.2b)
breadboards: 1

parts:
  Mod1 = KY-008 Laser Transmitter Module [package="Breakout board"]
  Part1 = Arduino Uno (Rev3) - ICSP
  J1 = Piezo Speaker
  R1 = Photocell (LDR) [package=THT]
  R2 = Resistor [tolerance=±5% resistance=220 package="0402 [SMD]"]

nets:
  N1: Mod1.S, Part1.5V, R2.Pin_0
  N2: Mod1.-, Part1.GND, J1.pin1, R1.pin_1
  N3: Part1.A0, R1.pin_0, R2.Pin_1
  N4: Part1.D5_PWM, J1.pin2

custom parts:
  KY-008 Laser Transmitter Module: KY-008 Laser Transmitter Module, emits a dot shaped red laser beam.
